# Fritzing sketch bench (saved by Fritzing 1.0.6)
breadboards: 1

parts:
  SOIC-8_clip = SOIC-8 clip
  ESP-Prog = ESP-Prog [package=THT]
  Lab_PSU = Lab PSU

nets:
  N1: SOIC-8_clip.CS#, ESP-Prog.JTAG-ESP_TMS-.1
  N2: SOIC-8_clip.DO, ESP-Prog.JAG-ESP-TDO-.1
  VCC: SOIC-8_clip.WP#, SOIC-8_clip.HOLD#, SOIC-8_clip.VCC, Lab_PSU.+3.3V
  GND: SOIC-8_clip.GND, ESP-Prog.JTAG-GND-9-.1, Lab_PSU.GND
  N3: SOIC-8_clip.DI, ESP-Prog.JTAG-ESP_TDI-.1
  N4: SOIC-8_clip.CLK, ESP-Prog.JTAG-ESP-TCK-.1

notes:
  No breadboard on the real bench: Dupont leads from the clip
  straight to the ESP-Prog header and the PSU terminals.
  ESP-Prog I/O jumper on 3.3 V, VDD (pin 1) open.
  PSU 3.3 V, limit 300 mA. Clip pin 1 on the chip's dot.
  Clip on/off only with the PSU off and USB unplugged.

custom parts:
  SOIC-8 clip: SOIC-8 test clip on a 25xx SPI flash, pin 1 bottom left.
  ESP-Prog: Espressif ESP-Prog board. ESP-Prog is one of Espressif’s development and debugging tools, with functions including automatic firmware downloading, serial communication, and JTAG online debugging. ESP-Prog's automatic firmware downloading and serial communication functions are supported on both the ESP8266 and ESP32 platforms, while the JTAG online debugging is supported only on the ESP32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
  Lab PSU: Current-limited bench supply, 3.3 V, limit 300 mA.
